# Fritzing sketch schema (saved by Fritzing 0.9.4)

parts:
  U1 = LuaNode32 / ESP32
  Součástka1 = Solar Cell
  Part1 = Solar Charge Controller [part_number="HGX Series Solar Charge Controller PWM" package=PWM-Model]
  M1 = INA3221 Triple Channel Current/Voltage Monitor Module [part_number="3221 Black"]
  Součástka15 = Adafruit SHT31-D [part_number="Adafruit #2857"]
  BAT1 = 12 battery [package=battery]
  Součástka16 = Solar Cell
  IC1 = Voltage Regulator [package=78xxl]
  BAT3 = Battery Holders [package=battery-aa]
  BAT2 = Battery Holders [package=battery-aa]
  A1 = X804
  R1 = Resistor [tolerance=±5% resistance=220 package="0402 [SMD]"]
  R2 = Resistor [tolerance=±5% resistance=220 package="0402 [SMD]"]

nets:
  N1: U1.VP, R1.Pin_0, R2.Pin_1
  GND: U1.GND, Part1.Connector_6, M1.GND, Součástka15.GND, IC1.GND, BAT3.-, BAT2.-, A1.Pin_1, A1.Pin_4, A1.Pin_5, R1.Pin_1
  VIN: U1.Vin, M1.VS, Součástka15.VCC, IC1.OUT
  N2: U1.D21, M1.SDA, Součástka15.SDA
  N3: U1.D22, M1.SCL, Součástka15.SCL
  N4: Součástka1.+, M1.VN1+, Součástka16.+
  N5: Součástka1.-, Part1.Connector_2, Součástka16.-
  N6: Part1.Connector_1, M1.VN1-
  N7: Part1.Connector_3, M1.VN2-
  N8: Part1.Connector_4, BAT1.-
  N9: Part1.Connector_5, IC1.IN
  N10: M1.VN3-, A1.Pin_6
  N11: M1.VN2+, BAT1.+
  N12: BAT3.+, A1.Pin_3
  N13: BAT2.+, A1.Pin_2, R2.Pin_0

notes:
  2x 18V 40W solar panel
  12V 60Ah battery
  INA3221 sensors
  12V -> 5V voltage regulator from PWM solar charger controller
  SHT31 temperature & humidi senzor
  200kΩ
  100kΩ
  Voltage divider 5V => 3.3V
  5V powerbank 60Ah
  YX850 5V Automatic Switching UPS. Takes 60mAh ona first battery
  5V output to load..

custom parts:
  LuaNode32 / ESP32: ESP32 based LuaNode32
  Solar Charge Controller: PWM-Solar Charge Controller
  INA3221 Triple Channel Current/Voltage Monitor Module: INA3221 Triple Channel Current/Voltage Monitor Module Links: INA3221 product information
  Adafruit SHT31-D: Sensirion Temperature/Humidity sensors are some of the finest & highest-accuracy devices you can get. And, finally we have some that have a true I2C interface for easy reading. The SHT31-D sensor has an excellent ±2% relative humidity and ±0.3°C accuracy for most uses. We now use the version with a PTFE filter, it'll stay clean while still allowing humidity measurements to work Unlike earlier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
  12 battery: 12V lead acid type battery, like the Husqvarna YTH2448 12V 35AH battery. This is the mini version 1/4 the size of the actual battery to be closer to typical breadboard parts (around 2in wide rathher than 7in). The pads in pcb are sized to accomidate up to 14ga wire (as these batterys will deliver high currents.)
  X804: This is a power outage automatic switch module for 12V-48V battery.
